// Logisim project riscv_cpus.circ as structural Verilog: 31 circuits, main circuit cpu_single_cycle
module cpu_single_cycle (
  input  [31:0] DataIn,
  input  RST,
  input  CLK,
  input  Hold,
  output [31:0] DataOut,
  output [31:0] Addr,
  output RW,
  output [1:0] DataAlign,
  output HLDA
);

  wire and_1_out, branch_comparator_1_tk, hold_unit_1_clk, not_1_out, not_2_out, or_1_out,
       sc_decode_control_1_addrsrc, sc_decode_control_1_br, sc_decode_control_1_exfunc3en,
       sc_decode_control_1_jp, sc_decode_control_1_opra, sc_decode_control_1_oprb, sc_decode_control_1_rfwe;
  wire [1:0] sc_decode_control_1_rfsrc;
  wire [2:0] sc_decode_control_1_instrfmt;
  wire [2:2] sc_decode_control_1_func3;
  wire [4:0] sc_decode_control_1_rd, sc_decode_control_1_rs1, sc_decode_control_1_rs2;
  wire [6:0] sc_decode_control_1_func7;
  wire [31:0] alu_1_res, data_aligner_1_dataout, fetch_unit_1_npc, fetch_unit_1_pc, imm_gen_1_imm,
       multiplexer_2_out, multiplexer_3_out, multiplexer_4_out, register_file_1_ra, sc_decode_control_1_instr;

  Multiplexer #(.disabled("Z"), .enable("true"), .width(32)) multiplexer_1 (
    .in0(fetch_unit_1_pc), .in1(alu_1_res), .out(Addr), .sel(sc_decode_control_1_addrsrc), .en(not_1_out));
  not not_1 (not_1_out, HLDA);
  fetch_unit fetch_unit_1 (
    .PC_Src(or_1_out), .En(not_2_out), .CLK(hold_unit_1_clk), .RST(RST), .PCTarget(alu_1_res),
    .NPC(fetch_unit_1_npc), .PC(fetch_unit_1_pc));
  not not_2 (not_2_out, sc_decode_control_1_addrsrc);
  sc_decode_control sc_decode_control_1 (
    .CLK(hold_unit_1_clk), .RST(RST), .InstrIn(DataIn), .InstrFmt(sc_decode_control_1_instrfmt),
    .JP(sc_decode_control_1_jp), .BR(sc_decode_control_1_br), .RFSrc(sc_decode_control_1_rfsrc),
    .RFWe(sc_decode_control_1_rfwe), .ExFunc3En(sc_decode_control_1_exfunc3en),
    .OprA(sc_decode_control_1_opra), .OprB(sc_decode_control_1_oprb), .AddrSrc(sc_decode_control_1_addrsrc),
    .RW(RW), .Rd(sc_decode_control_1_rd), .Func3({sc_decode_control_1_func3[2], DataAlign}),
    .Rs1(sc_decode_control_1_rs1), .Rs2(sc_decode_control_1_rs2), .Func7(sc_decode_control_1_func7),
    .Instr(sc_decode_control_1_instr));
  register_file register_file_1 (
    .We(sc_decode_control_1_rfwe), .Rs2(sc_decode_control_1_rs2), .RST(RST), .CLK(hold_unit_1_clk),
    .Rs1(sc_decode_control_1_rs1), .Rd(sc_decode_control_1_rd), .DataIn(multiplexer_4_out), .Rb(DataOut),
    .Ra(register_file_1_ra));
  imm_gen imm_gen_1 (.InstrFmt(sc_decode_control_1_instrfmt), .Instr(sc_decode_control_1_instr), .Imm(imm_gen_1_imm));
  branch_comparator branch_comparator_1 (
    .Func3({sc_decode_control_1_func3[2], DataAlign}), .A(register_file_1_ra), .B(DataOut),
    .TK(branch_comparator_1_tk));
  Multiplexer #(.width(32)) multiplexer_2 (
    .in0(register_file_1_ra), .in1(fetch_unit_1_pc), .out(multiplexer_2_out), .sel(sc_decode_control_1_opra));
  Multiplexer #(.width(32)) multiplexer_3 (
    .in0(DataOut), .in1(imm_gen_1_imm), .out(multiplexer_3_out), .sel(sc_decode_control_1_oprb));
  and and_1 (and_1_out, sc_decode_control_1_br, branch_comparator_1_tk);
  alu alu_1 (
    .Func3En(sc_decode_control_1_exfunc3en), .InstrFmt(sc_decode_control_1_instrfmt),
    .Func3({sc_decode_control_1_func3[2], DataAlign}), .B(multiplexer_3_out), .A(multiplexer_2_out),
    .Func7(sc_decode_control_1_func7), .Res(alu_1_res));
  or or_1 (or_1_out, sc_decode_control_1_jp, and_1_out);
  data_aligner data_aligner_1 (
    .Func3({sc_decode_control_1_func3[2], DataAlign}), .DataIn(DataIn), .DataOut(data_aligner_1_dataout));
  Multiplexer #(.select(2), .width(32)) multiplexer_4 (
    .in0(data_aligner_1_dataout), .in1(fetch_unit_1_npc), .in2(alu_1_res), .in3(multiplexer_3_out),
    .out(multiplexer_4_out), .sel(sc_decode_control_1_rfsrc));
  hold_unit hold_unit_1 (
    .nRDY(sc_decode_control_1_addrsrc), .Hold(Hold), .RST(RST), .CLKIn(CLK), .HLDA(HLDA),
    .CLK(hold_unit_1_clk));
endmodule

module cpu_multi_cycle (
  input  [31:0] DataIn,
  input  RST,
  input  CLK,
  input  Hold,
  output [1:0] DataAlign,
  output [31:0] Addr,
  output RW,
  output [31:0] DataOut,
  output HLDA
);

  wire and_1_out, branch_comparator_1_tk, hold_unit_1_clk, mc_decode_control_1_addrsrc,
       mc_decode_control_1_br, mc_decode_control_1_exfunc3en, mc_decode_control_1_jp,
       mc_decode_control_1_opra, mc_decode_control_1_oprb, mc_decode_control_1_pcld,
       mc_decode_control_1_rfwe, not_1_out, or_1_out;
  wire [1:0] mc_decode_control_1_rfsrc;
  wire [2:0] mc_decode_control_1_instrfmt;
  wire [2:2] mc_decode_control_1_func3;
  wire [4:0] mc_decode_control_1_rd, mc_decode_control_1_rs1, mc_decode_control_1_rs2;
  wire [6:0] mc_decode_control_1_func7;
  wire [31:0] alu_1_res, data_aligner_1_dataout, fetch_unit_1_npc, fetch_unit_1_pc, imm_gen_1_imm,
       mc_decode_control_1_instr, mc_hold_reg_1_dataout, mc_hold_reg_2_dataout, mc_hold_reg_3_dataout,
       mc_hold_reg_4_dataout, multiplexer_2_out, multiplexer_3_out, multiplexer_4_out, register_file_1_ra;

  Multiplexer #(.disabled("Z"), .enable("true"), .width(32)) multiplexer_1 (
    .in0(fetch_unit_1_pc), .in1(mc_hold_reg_3_dataout), .out(Addr), .sel(mc_decode_control_1_addrsrc),
    .en(not_1_out));
  not not_1 (not_1_out, HLDA);
  fetch_unit fetch_unit_1 (
    .PC_Src(or_1_out), .En(mc_decode_control_1_pcld), .CLK(hold_unit_1_clk), .RST(RST), .PCTarget(alu_1_res),
    .NPC(fetch_unit_1_npc), .PC(fetch_unit_1_pc));
  mc_decode_control mc_decode_control_1 (
    .CLK(hold_unit_1_clk), .RST(RST), .InstrIn(DataIn), .Instr(mc_decode_control_1_instr),
    .Func7(mc_decode_control_1_func7), .Rs2(mc_decode_control_1_rs2), .Rs1(mc_decode_control_1_rs1),
    .Func3({mc_decode_control_1_func3[2], DataAlign}), .Rd(mc_decode_control_1_rd),
    .PcLd(mc_decode_control_1_pcld), .InstrFmt(mc_decode_control_1_instrfmt), .JP(mc_decode_control_1_jp),
    .BR(mc_decode_control_1_br), .RFSrc(mc_decode_control_1_rfsrc), .RFWe(mc_decode_control_1_rfwe),
    .ExFunc3En(mc_decode_control_1_exfunc3en), .OprA(mc_decode_control_1_opra),
    .OprB(mc_decode_control_1_oprb), .AddrSrc(mc_decode_control_1_addrsrc), .RW(RW));
  register_file register_file_1 (
    .We(mc_decode_control_1_rfwe), .Rs2(mc_decode_control_1_rs2), .RST(RST), .CLK(hold_unit_1_clk),
    .Rs1(mc_decode_control_1_rs1), .Rd(mc_decode_control_1_rd), .DataIn(multiplexer_4_out), .Rb(DataOut),
    .Ra(register_file_1_ra));
  imm_gen imm_gen_1 (.InstrFmt(mc_decode_control_1_instrfmt), .Instr(mc_decode_control_1_instr), .Imm(imm_gen_1_imm));
  branch_comparator branch_comparator_1 (
    .Func3({mc_decode_control_1_func3[2], DataAlign}), .A(register_file_1_ra), .B(DataOut),
    .TK(branch_comparator_1_tk));
  Multiplexer #(.width(32)) multiplexer_2 (
    .in0(register_file_1_ra), .in1(fetch_unit_1_pc), .out(multiplexer_2_out), .sel(mc_decode_control_1_opra));
  mc_hold_reg mc_hold_reg_1 (
    .CLK(hold_unit_1_clk), .RST(RST), .DataIn(multiplexer_2_out), .DataOut(mc_hold_reg_1_dataout));
  Multiplexer #(.width(32)) multiplexer_3 (
    .in0(DataOut), .in1(imm_gen_1_imm), .out(multiplexer_3_out), .sel(mc_decode_control_1_oprb));
  mc_hold_reg mc_hold_reg_2 (
    .CLK(hold_unit_1_clk), .RST(RST), .DataIn(multiplexer_3_out), .DataOut(mc_hold_reg_2_dataout));
  and and_1 (and_1_out, mc_decode_control_1_br, branch_comparator_1_tk);
  or or_1 (or_1_out, mc_decode_control_1_jp, and_1_out);
  alu alu_1 (
    .Func3En(mc_decode_control_1_exfunc3en), .InstrFmt(mc_decode_control_1_instrfmt),
    .Func3({mc_decode_control_1_func3[2], DataAlign}), .B(mc_hold_reg_2_dataout), .A(mc_hold_reg_1_dataout),
    .Func7(mc_decode_control_1_func7), .Res(alu_1_res));
  mc_hold_reg mc_hold_reg_3 (.CLK(hold_unit_1_clk), .RST(RST), .DataIn(alu_1_res), .DataOut(mc_hold_reg_3_dataout));
  data_aligner data_aligner_1 (
    .Func3({mc_decode_control_1_func3[2], DataAlign}), .DataIn(DataIn), .DataOut(data_aligner_1_dataout));
  mc_hold_reg mc_hold_reg_4 (
    .CLK(hold_unit_1_clk), .RST(RST), .DataIn(data_aligner_1_dataout), .DataOut(mc_hold_reg_4_dataout));
  Multiplexer #(.select(2), .width(32)) multiplexer_4 (
    .in0(mc_hold_reg_4_dataout), .in1(fetch_unit_1_npc), .in2(mc_hold_reg_3_dataout),
    .in3(mc_hold_reg_2_dataout), .out(multiplexer_4_out), .sel(mc_decode_control_1_rfsrc));
  hold_unit hold_unit_1 (
    .nRDY(mc_decode_control_1_addrsrc), .Hold(Hold), .RST(RST), .CLKIn(CLK), .HLDA(HLDA),
    .CLK(hold_unit_1_clk));
endmodule

module cpu_pipeined (
  input  [31:0] DataIn,
  input  RST,
  input  CLK,
  input  Hold,
  output [31:0] Addr,
  output HLDA,
  output [1:0] DataAlign,
  output [31:0] DataOut,
  output RW
);

  wire and_1_out, and_2_out, branch_comparator_1_tk, forwarding_unit_1_fwda, forwarding_unit_1_fwdb,
       hold_unit_1_clk, not_1_out, not_2_out, or_1_out, pipe_de_ex_1_br, pipe_de_ex_1_exfunc3en,
       pipe_de_ex_1_jp, pipe_de_ex_1_opra, pipe_de_ex_1_oprb, pipe_ex_ma_1_addrsrc, pipe_ex_ma_1_jp_br,
       pipe_ex_ma_1_lui, pipe_ex_ma_1_rfwe, pipe_flush_1_flush, pipe_ma_wb_1_rfwe;
  wire [1:0] pipe_ma_wb_1_rfsrc;
  wire [2:0] pipe_de_ex_1_func3, pipe_de_ex_1_instrfmt;
  wire [2:2] pipe_ex_ma_1_func3;
  wire [4:0] pipe_de_ex_1_rd, pipe_de_ex_1_rs1, pipe_de_ex_1_rs2, pipe_ex_ma_1_rd, pipe_if_de_1_rs1,
       pipe_if_de_1_rs2, pipe_ma_wb_1_rd;
  wire [6:0] pipe_de_ex_1_func7;
  wire [12:0] pipe_de_ex_1_ctrlword, pipe_ex_ma_1_ctrlword, pl_decode_1_ctrlword;
  wire [31:0] alu_1_res, data_aligner_1_dataout, fetch_unit_1_npc, fetch_unit_1_pc, forwarding_unit_1_a,
       forwarding_unit_1_b, fwd_mux_1_aluopr, fwd_mux_1_bropr, fwd_mux_2_aluopr, fwd_mux_2_bropr,
       multiplexer_2_out, multiplexer_3_out, multiplexer_4_out, pipe_de_ex_1_imm, pipe_de_ex_1_npc,
       pipe_de_ex_1_pc, pipe_de_ex_1_ra, pipe_de_ex_1_rb, pipe_ex_ma_1_alures, pipe_ex_ma_1_imm,
       pipe_ex_ma_1_npc, pipe_if_de_1_instr, pipe_if_de_1_npc, pipe_if_de_1_pc, pipe_ma_wb_1_alures,
       pipe_ma_wb_1_imm, pipe_ma_wb_1_memdata, pipe_ma_wb_1_npc, pl_decode_1_imm, register_file_1_ra,
       register_file_1_rb;

  Multiplexer #(.disabled("Z"), .enable("true"), .width(32)) multiplexer_1 (
    .in0(fetch_unit_1_pc), .in1(pipe_ex_ma_1_alures), .out(Addr), .sel(pipe_ex_ma_1_addrsrc), .en(not_1_out));
  not not_1 (not_1_out, HLDA);
  fetch_unit fetch_unit_1 (
    .PC_Src(pipe_ex_ma_1_jp_br), .En(not_2_out), .CLK(hold_unit_1_clk), .RST(RST),
    .PCTarget(pipe_ex_ma_1_alures), .NPC(fetch_unit_1_npc), .PC(fetch_unit_1_pc));
  not not_2 (not_2_out, pipe_ex_ma_1_addrsrc);
  pipe_if_de pipe_if_de_1 (
    .AddrSrc(pipe_ex_ma_1_addrsrc), .CLK(hold_unit_1_clk), .RST(pipe_flush_1_flush), .PCIn(fetch_unit_1_pc),
    .NPCIn(fetch_unit_1_npc), .InstrIn(DataIn), .Instr(pipe_if_de_1_instr), .Rs1(pipe_if_de_1_rs1),
    .Rs2(pipe_if_de_1_rs2), .PC(pipe_if_de_1_pc), .NPC(pipe_if_de_1_npc));
  register_file register_file_1 (
    .We(pipe_ma_wb_1_rfwe), .Rs2(pipe_if_de_1_rs2), .RST(RST), .CLK(hold_unit_1_clk), .Rs1(pipe_if_de_1_rs1),
    .Rd(pipe_ma_wb_1_rd), .DataIn(multiplexer_4_out), .Rb(register_file_1_rb), .Ra(register_file_1_ra));
  pl_decode pl_decode_1 (.Instr(pipe_if_de_1_instr), .CtrlWord(pl_decode_1_ctrlword), .Imm(pl_decode_1_imm));
  pipe_de_ex pipe_de_ex_1 (
    .CLK(hold_unit_1_clk), .RST(pipe_flush_1_flush), .CtrlWordIn(pl_decode_1_ctrlword),
    .RbIn(register_file_1_rb), .Instr(pipe_if_de_1_instr), .PCIn(pipe_if_de_1_pc), .NPCIn(pipe_if_de_1_npc),
    .RaIn(register_file_1_ra), .ImmIn(pl_decode_1_imm), .Rb(pipe_de_ex_1_rb), .Rd(pipe_de_ex_1_rd),
    .Func3(pipe_de_ex_1_func3), .Rs1(pipe_de_ex_1_rs1), .Rs2(pipe_de_ex_1_rs2), .Func7(pipe_de_ex_1_func7),
    .PC(pipe_de_ex_1_pc), .NPC(pipe_de_ex_1_npc), .Ra(pipe_de_ex_1_ra), .Imm(pipe_de_ex_1_imm),
    .CtrlWord(pipe_de_ex_1_ctrlword), .InstrFmt(pipe_de_ex_1_instrfmt), .JP(pipe_de_ex_1_jp),
    .BR(pipe_de_ex_1_br), .ExFunc3En(pipe_de_ex_1_exfunc3en), .OprA(pipe_de_ex_1_opra),
    .OprB(pipe_de_ex_1_oprb));
  forwarding_unit forwarding_unit_1 (
    .WB_RFWe(pipe_ma_wb_1_rfwe), .MA_RFWe(pipe_ex_ma_1_rfwe), .Rs1(pipe_de_ex_1_rs1),
    .WB_Rd(pipe_ma_wb_1_rd), .MA_Rd(pipe_ex_ma_1_rd), .Rs2(pipe_de_ex_1_rs2), .WBData(multiplexer_4_out),
    .MAData(multiplexer_3_out), .B(forwarding_unit_1_b), .FwdA(forwarding_unit_1_fwda),
    .FwdB(forwarding_unit_1_fwdb), .A(forwarding_unit_1_a));
  pipe_flush pipe_flush_1 (.JP_BR(pipe_ex_ma_1_jp_br), .Clk(hold_unit_1_clk), .Rst(RST), .Flush(pipe_flush_1_flush));
  fwd_mux fwd_mux_1 (
    .FwdEn(forwarding_unit_1_fwda), .ForceOpr2(pipe_de_ex_1_opra), .Opr2(pipe_de_ex_1_pc),
    .Opr1(pipe_de_ex_1_ra), .FwdData(forwarding_unit_1_a), .BROpr(fwd_mux_1_bropr), .AluOpr(fwd_mux_1_aluopr));
  fwd_mux fwd_mux_2 (
    .FwdEn(forwarding_unit_1_fwdb), .ForceOpr2(pipe_de_ex_1_oprb), .Opr2(pipe_de_ex_1_imm),
    .Opr1(pipe_de_ex_1_rb), .FwdData(forwarding_unit_1_b), .BROpr(fwd_mux_2_bropr), .AluOpr(fwd_mux_2_aluopr));
  branch_comparator branch_comparator_1 (
    .Func3(pipe_de_ex_1_func3), .A(fwd_mux_1_bropr), .B(fwd_mux_2_bropr), .TK(branch_comparator_1_tk));
  alu alu_1 (
    .Func3En(pipe_de_ex_1_exfunc3en), .InstrFmt(pipe_de_ex_1_instrfmt), .Func3(pipe_de_ex_1_func3),
    .B(fwd_mux_2_aluopr), .A(fwd_mux_1_aluopr), .Func7(pipe_de_ex_1_func7), .Res(alu_1_res));
  or or_1 (or_1_out, pipe_de_ex_1_jp, and_1_out);
  and and_1 (and_1_out, pipe_de_ex_1_br, branch_comparator_1_tk);
  pipe_ex_ma pipe_ex_ma_1 (
    .CLK(hold_unit_1_clk), .RST(RST), .JP_BR_In(or_1_out), .RdIn(pipe_de_ex_1_rd),
    .CtrlWordIn(pipe_de_ex_1_ctrlword), .Func3In(pipe_de_ex_1_func3), .AluResIn(alu_1_res),
    .RbIn(fwd_mux_2_bropr), .NPCIn(pipe_de_ex_1_npc), .ImmIn(fwd_mux_2_aluopr), .AluRes(pipe_ex_ma_1_alures),
    .Func3({pipe_ex_ma_1_func3[2], DataAlign}), .Rb(DataOut), .NPC(pipe_ex_ma_1_npc), .Imm(pipe_ex_ma_1_imm),
    .Rd(pipe_ex_ma_1_rd), .JP_BR(pipe_ex_ma_1_jp_br), .CtrlWord(pipe_ex_ma_1_ctrlword),
    .AddrSrc(pipe_ex_ma_1_addrsrc), .RW(RW), .RfWe(pipe_ex_ma_1_rfwe), .lui(pipe_ex_ma_1_lui));
  Multiplexer #(.width(32)) multiplexer_2 (
    .in0(pipe_ex_ma_1_alures), .in1(pipe_ex_ma_1_imm), .out(multiplexer_2_out), .sel(pipe_ex_ma_1_lui));
  and and_2 (and_2_out, pipe_ex_ma_1_addrsrc, ~RW);  // AND_Gate
  data_aligner data_aligner_1 (
    .Func3({pipe_ex_ma_1_func3[2], DataAlign}), .DataIn(DataIn), .DataOut(data_aligner_1_dataout));
  Multiplexer #(.width(32)) multiplexer_3 (
    .in0(multiplexer_2_out), .in1(data_aligner_1_dataout), .out(multiplexer_3_out), .sel(and_2_out));
  pipe_ma_wb pipe_ma_wb_1 (
    .CLK(hold_unit_1_clk), .RST(RST), .ImmIn(pipe_ex_ma_1_imm), .RdIn(pipe_ex_ma_1_rd),
    .CtrlWordIn(pipe_ex_ma_1_ctrlword), .AluResIn(multiplexer_2_out), .NPCIn(pipe_ex_ma_1_npc),
    .MemDataIn(data_aligner_1_dataout), .AluRes(pipe_ma_wb_1_alures), .NPC(pipe_ma_wb_1_npc),
    .Imm(pipe_ma_wb_1_imm), .Rd(pipe_ma_wb_1_rd), .RFSrc(pipe_ma_wb_1_rfsrc), .RFWe(pipe_ma_wb_1_rfwe),
    .MemData(pipe_ma_wb_1_memdata));
  Multiplexer #(.select(2), .width(32)) multiplexer_4 (
    .in0(pipe_ma_wb_1_memdata), .in1(pipe_ma_wb_1_npc), .in2(pipe_ma_wb_1_alures), .in3(pipe_ma_wb_1_imm),
    .out(multiplexer_4_out), .sel(pipe_ma_wb_1_rfsrc));
  hold_unit hold_unit_1 (
    .nRDY(pipe_ex_ma_1_addrsrc), .Hold(Hold), .RST(RST), .CLKIn(CLK), .HLDA(HLDA), .CLK(hold_unit_1_clk));
endmodule

module cpu_pipelined_bp (
  input  [31:0] DataIn,
  input  RST,
  input  CLK,
  input  Hold,
  output [31:0] Addr,
  output HLDA,
  output [1:0] DataAlign,
  output [31:0] DataOut,
  output RW
);

  wire and_1_out, bp_pipe_de_ex_1_exfunc3en, bp_pipe_de_ex_1_opra, bp_pipe_de_ex_1_oprb,
       bp_pipe_ex_ma_1_addrsrc, bp_pipe_ex_ma_1_br, bp_pipe_ex_ma_1_branchtaken, bp_pipe_ex_ma_1_eval_jp_br,
       bp_pipe_ex_ma_1_lui, bp_pipe_ex_ma_1_rfwe, branch_comparator_1_tk, branch_predictor_1_flush,
       branch_predictor_1_pc_src, forwarding_unit_1_fwda, forwarding_unit_1_fwdb, hold_unit_1_clk, not_1_out,
       not_2_out, pipe_ma_wb_1_rfwe;
  wire [1:0] pipe_ma_wb_1_rfsrc;
  wire [2:0] bp_pipe_de_ex_1_func3, bp_pipe_de_ex_1_instrfmt;
  wire [2:2] bp_pipe_ex_ma_1_func3;
  wire [4:0] bp_pipe_de_ex_1_rd, bp_pipe_de_ex_1_rs1, bp_pipe_de_ex_1_rs2, bp_pipe_ex_ma_1_rd,
       pipe_if_de_1_rs1, pipe_if_de_1_rs2, pipe_ma_wb_1_rd;
  wire [6:0] bp_pipe_de_ex_1_func7;
  wire [12:0] bp_pipe_de_ex_1_ctrlword, bp_pipe_ex_ma_1_ctrlword, pl_decode_1_ctrlword;
  wire [31:0] alu_1_res, bp_pipe_de_ex_1_imm, bp_pipe_de_ex_1_npc, bp_pipe_de_ex_1_pc, bp_pipe_de_ex_1_ra,
       bp_pipe_de_ex_1_rb, bp_pipe_ex_ma_1_alures, bp_pipe_ex_ma_1_imm, bp_pipe_ex_ma_1_npc,
       bp_pipe_ex_ma_1_pc, branch_predictor_1_predicted_target, data_aligner_1_dataout, fetch_unit_1_npc,
       fetch_unit_1_pc, forwarding_unit_1_a, forwarding_unit_1_b, fwd_mux_1_aluopr, fwd_mux_1_bropr,
       fwd_mux_2_aluopr, fwd_mux_2_bropr, multiplexer_2_out, multiplexer_3_out, multiplexer_4_out,
       pipe_if_de_1_instr, pipe_if_de_1_npc, pipe_if_de_1_pc, pipe_ma_wb_1_alures, pipe_ma_wb_1_imm,
       pipe_ma_wb_1_memdata, pipe_ma_wb_1_npc, pl_decode_1_imm, register_file_1_ra, register_file_1_rb;

  Multiplexer #(.disabled("Z"), .enable("true"), .width(32)) multiplexer_1 (
    .in0(fetch_unit_1_pc), .in1(bp_pipe_ex_ma_1_alures), .out(Addr), .sel(bp_pipe_ex_ma_1_addrsrc),
    .en(not_1_out));
  not not_1 (not_1_out, HLDA);
  fetch_unit fetch_unit_1 (
    .PC_Src(branch_predictor_1_pc_src), .En(not_2_out), .CLK(hold_unit_1_clk), .RST(RST),
    .PCTarget(branch_predictor_1_predicted_target), .NPC(fetch_unit_1_npc), .PC(fetch_unit_1_pc));
  not not_2 (not_2_out, bp_pipe_ex_ma_1_addrsrc);
  pipe_if_de pipe_if_de_1 (
    .AddrSrc(bp_pipe_ex_ma_1_addrsrc), .CLK(hold_unit_1_clk), .RST(branch_predictor_1_flush),
    .PCIn(fetch_unit_1_pc), .NPCIn(fetch_unit_1_npc), .InstrIn(DataIn), .Instr(pipe_if_de_1_instr),
    .Rs1(pipe_if_de_1_rs1), .Rs2(pipe_if_de_1_rs2), .PC(pipe_if_de_1_pc), .NPC(pipe_if_de_1_npc));
  register_file register_file_1 (
    .We(pipe_ma_wb_1_rfwe), .Rs2(pipe_if_de_1_rs2), .RST(RST), .CLK(hold_unit_1_clk), .Rs1(pipe_if_de_1_rs1),
    .Rd(pipe_ma_wb_1_rd), .DataIn(multiplexer_4_out), .Rb(register_file_1_rb), .Ra(register_file_1_ra));
  pl_decode pl_decode_1 (.Instr(pipe_if_de_1_instr), .CtrlWord(pl_decode_1_ctrlword), .Imm(pl_decode_1_imm));
  bp_pipe_de_ex bp_pipe_de_ex_1 (
    .CLK(hold_unit_1_clk), .RST(branch_predictor_1_flush), .CtrlWordIn(pl_decode_1_ctrlword),
    .RbIn(register_file_1_rb), .Instr(pipe_if_de_1_instr), .PCIn(pipe_if_de_1_pc), .NPCIn(pipe_if_de_1_npc),
    .ImmIn(pl_decode_1_imm), .RaIn(register_file_1_ra), .Rb(bp_pipe_de_ex_1_rb), .Rd(bp_pipe_de_ex_1_rd),
    .Func3(bp_pipe_de_ex_1_func3), .Rs1(bp_pipe_de_ex_1_rs1), .Rs2(bp_pipe_de_ex_1_rs2),
    .Func7(bp_pipe_de_ex_1_func7), .PC(bp_pipe_de_ex_1_pc), .NPC(bp_pipe_de_ex_1_npc),
    .Imm(bp_pipe_de_ex_1_imm), .CtrlWord(bp_pipe_de_ex_1_ctrlword), .InstrFmt(bp_pipe_de_ex_1_instrfmt),
    .ExFunc3En(bp_pipe_de_ex_1_exfunc3en), .OprA(bp_pipe_de_ex_1_opra), .OprB(bp_pipe_de_ex_1_oprb),
    .Ra(bp_pipe_de_ex_1_ra));
  forwarding_unit forwarding_unit_1 (
    .WB_RFWe(pipe_ma_wb_1_rfwe), .MA_RFWe(bp_pipe_ex_ma_1_rfwe), .Rs1(bp_pipe_de_ex_1_rs1),
    .WB_Rd(pipe_ma_wb_1_rd), .MA_Rd(bp_pipe_ex_ma_1_rd), .Rs2(bp_pipe_de_ex_1_rs2),
    .WBData(multiplexer_4_out), .MAData(multiplexer_3_out), .B(forwarding_unit_1_b),
    .FwdA(forwarding_unit_1_fwda), .FwdB(forwarding_unit_1_fwdb), .A(forwarding_unit_1_a));
  branch_predictor branch_predictor_1 (
    .Is_Branch(bp_pipe_ex_ma_1_br), .Is_Taken(bp_pipe_ex_ma_1_branchtaken),
    .Eval(bp_pipe_ex_ma_1_eval_jp_br), .CLK(hold_unit_1_clk), .RST(RST), .NPC(bp_pipe_ex_ma_1_npc),
    .PC(fetch_unit_1_pc), .Eval_PC(bp_pipe_ex_ma_1_pc), .Alu_Res(bp_pipe_ex_ma_1_alures),
    .Predicted_Target(branch_predictor_1_predicted_target), .PC_Src(branch_predictor_1_pc_src),
    .Flush(branch_predictor_1_flush));
  fwd_mux fwd_mux_1 (
    .FwdEn(forwarding_unit_1_fwda), .ForceOpr2(bp_pipe_de_ex_1_opra), .Opr2(bp_pipe_de_ex_1_pc),
    .Opr1(bp_pipe_de_ex_1_ra), .FwdData(forwarding_unit_1_a), .BROpr(fwd_mux_1_bropr),
    .AluOpr(fwd_mux_1_aluopr));
  fwd_mux fwd_mux_2 (
    .FwdEn(forwarding_unit_1_fwdb), .ForceOpr2(bp_pipe_de_ex_1_oprb), .Opr2(bp_pipe_de_ex_1_imm),
    .Opr1(bp_pipe_de_ex_1_rb), .FwdData(forwarding_unit_1_b), .BROpr(fwd_mux_2_bropr),
    .AluOpr(fwd_mux_2_aluopr));
  branch_comparator branch_comparator_1 (
    .Func3(bp_pipe_de_ex_1_func3), .A(fwd_mux_1_bropr), .B(fwd_mux_2_bropr), .TK(branch_comparator_1_tk));
  alu alu_1 (
    .Func3En(bp_pipe_de_ex_1_exfunc3en), .InstrFmt(bp_pipe_de_ex_1_instrfmt), .Func3(bp_pipe_de_ex_1_func3),
    .B(fwd_mux_2_aluopr), .A(fwd_mux_1_aluopr), .Func7(bp_pipe_de_ex_1_func7), .Res(alu_1_res));
  bp_pipe_ex_ma bp_pipe_ex_ma_1 (
    .CLK(hold_unit_1_clk), .BranchTakenIn(branch_comparator_1_tk), .RST(RST), .RdIn(bp_pipe_de_ex_1_rd),
    .Func3In(bp_pipe_de_ex_1_func3), .CtrlWordIn(bp_pipe_de_ex_1_ctrlword), .AluResIn(alu_1_res),
    .RbIn(fwd_mux_2_bropr), .NPCIn(bp_pipe_de_ex_1_npc), .ImmIn(fwd_mux_2_aluopr), .PCIn(bp_pipe_de_ex_1_pc),
    .AluRes(bp_pipe_ex_ma_1_alures), .Func3({bp_pipe_ex_ma_1_func3[2], DataAlign}), .Rb(DataOut),
    .NPC(bp_pipe_ex_ma_1_npc), .Imm(bp_pipe_ex_ma_1_imm), .Rd(bp_pipe_ex_ma_1_rd), .PC(bp_pipe_ex_ma_1_pc),
    .BranchTaken(bp_pipe_ex_ma_1_branchtaken), .AddrSrc(bp_pipe_ex_ma_1_addrsrc), .RW(RW),
    .RfWe(bp_pipe_ex_ma_1_rfwe), .lui(bp_pipe_ex_ma_1_lui), .BR(bp_pipe_ex_ma_1_br),
    .CtrlWord(bp_pipe_ex_ma_1_ctrlword), .Eval_JP_BR(bp_pipe_ex_ma_1_eval_jp_br));
  data_aligner data_aligner_1 (
    .Func3({bp_pipe_ex_ma_1_func3[2], DataAlign}), .DataIn(DataIn), .DataOut(data_aligner_1_dataout));
  Multiplexer #(.width(32)) multiplexer_2 (
    .in0(bp_pipe_ex_ma_1_alures), .in1(bp_pipe_ex_ma_1_imm), .out(multiplexer_2_out),
    .sel(bp_pipe_ex_ma_1_lui));
  and and_1 (and_1_out, bp_pipe_ex_ma_1_addrsrc, ~RW);  // AND_Gate
  Multiplexer #(.width(32)) multiplexer_3 (
    .in0(multiplexer_2_out), .in1(data_aligner_1_dataout), .out(multiplexer_3_out), .sel(and_1_out));
  pipe_ma_wb pipe_ma_wb_1 (
    .CLK(hold_unit_1_clk), .RST(RST), .ImmIn(bp_pipe_ex_ma_1_imm), .RdIn(bp_pipe_ex_ma_1_rd),
    .CtrlWordIn(bp_pipe_ex_ma_1_ctrlword), .AluResIn(multiplexer_2_out), .NPCIn(bp_pipe_ex_ma_1_npc),
    .MemDataIn(data_aligner_1_dataout), .AluRes(pipe_ma_wb_1_alures), .NPC(pipe_ma_wb_1_npc),
    .Imm(pipe_ma_wb_1_imm), .Rd(pipe_ma_wb_1_rd), .RFSrc(pipe_ma_wb_1_rfsrc), .RFWe(pipe_ma_wb_1_rfwe),
    .MemData(pipe_ma_wb_1_memdata));
  Multiplexer #(.select(2), .width(32)) multiplexer_4 (
    .in0(pipe_ma_wb_1_memdata), .in1(pipe_ma_wb_1_npc), .in2(pipe_ma_wb_1_alures), .in3(pipe_ma_wb_1_imm),
    .out(multiplexer_4_out), .sel(pipe_ma_wb_1_rfsrc));
  hold_unit hold_unit_1 (
    .nRDY(bp_pipe_ex_ma_1_addrsrc), .Hold(Hold), .RST(RST), .CLKIn(CLK), .HLDA(HLDA), .CLK(hold_unit_1_clk));
endmodule

module alu (
  input  [31:0] A,
  input  [31:0] B,
  input  [2:0] InstrFmt,
  input  [6:0] Func7,
  input  [2:0] Func3,
  input  Func3En,
  output [31:0] Res
);

  wire alu_ctrl_1_alt, comparator_1_lt, comparator_2_lt;
  wire [3:0] alu_ctrl_1_func;
  wire [31:0] adder_1_out, and_1_out, bit_extender_7_out, bit_extender_8_out, divider_1_out, divider_1_rem,
       divider_2_out, divider_2_rem, multiplexer_1_out, multiplexer_2_out, multiplier_1_out, or_1_out,
       shifter_1_out, shifter_2_out, shifter_3_out, subtractor_1_out, xor_1_out;
  wire [32:0] bit_extender_1_out, bit_extender_2_out, bit_extender_3_out, bit_extender_4_out,
       bit_extender_5_out, bit_extender_6_out, multiplier_2_out, multiplier_3_out, multiplier_4_out;

  alu_ctrl alu_ctrl_1 (
    .Func3En(Func3En), .InstrFmt(InstrFmt), .Func3(Func3), .Func7(Func7), .Alt(alu_ctrl_1_alt),
    .Func(alu_ctrl_1_func));
  Adder #(.width(32)) adder_1 (.a(A), .b(B), .out(adder_1_out));  // open: cin, cout
  Subtractor #(.width(32)) subtractor_1 (.a(A), .b(B), .out(subtractor_1_out));  // open: bin, bout
  Shifter #(.width(32)) shifter_1 (.in(A), .\dist (B[4:0]), .out(shifter_1_out));
  Comparator #(.width(32)) comparator_1 (.a(A), .b(B), .lt(comparator_1_lt));  // open: gt, eq
  Comparator #(.mode("unsigned"), .width(32)) comparator_2 (.a(A), .b(B), .lt(comparator_2_lt));  // open: gt, eq
  assign xor_1_out = A ^ B;  // XOR_Gate xor_1, 32 bits wide
  Shifter #(.shift("lr"), .width(32)) shifter_2 (.in(A), .\dist (B[4:0]), .out(shifter_2_out));
  Shifter #(.shift("ar"), .width(32)) shifter_3 (.in(A), .\dist (B[4:0]), .out(shifter_3_out));
  assign or_1_out = A | B;  // OR_Gate or_1, 32 bits wide
  assign and_1_out = A & B;  // AND_Gate and_1, 32 bits wide
  Multiplier #(.width(32)) multiplier_1 (.a(A), .b(B), .out(multiplier_1_out));  // open: cin, cout
  assign bit_extender_1_out = {{1{A[31]}}, A};  // Bit_Extender bit_extender_1
  assign bit_extender_2_out = {{1{B[31]}}, B};  // Bit_Extender bit_extender_2
  assign bit_extender_3_out = {{1{1'b0}}, A};  // Bit_Extender bit_extender_3
  assign bit_extender_4_out = {{1{1'b0}}, B};  // Bit_Extender bit_extender_4
  assign bit_extender_5_out = {{1{A[31]}}, A};  // Bit_Extender bit_extender_5
  assign bit_extender_6_out = {{1{1'b0}}, B};  // Bit_Extender bit_extender_6
  Divider #(.mode("twosComplement"), .width(32)) divider_1 (
    .a(A), .b(B), .out(divider_1_out), .rem(divider_1_rem));  // open: upper
  Divider #(.width(32)) divider_2 (.a(A), .b(B), .out(divider_2_out), .rem(divider_2_rem));  // open: upper
  Multiplexer #(.width(32)) multiplexer_1 (
    .in0(adder_1_out), .in1(subtractor_1_out), .out(multiplexer_1_out), .sel(alu_ctrl_1_alt));
  assign bit_extender_7_out = {{31{1'b0}}, comparator_1_lt};  // Bit_Extender bit_extender_7
  assign bit_extender_8_out = {{31{1'b0}}, comparator_2_lt};  // Bit_Extender bit_extender_8
  Multiplexer #(.width(32)) multiplexer_2 (
    .in0(shifter_2_out), .in1(shifter_3_out), .out(multiplexer_2_out), .sel(alu_ctrl_1_alt));
  Multiplier #(.width(33)) multiplier_2 (
    .a(bit_extender_1_out), .b(bit_extender_2_out), .out(multiplier_2_out));  // open: cin, cout
  Multiplier #(.width(33)) multiplier_3 (
    .a(bit_extender_3_out), .b(bit_extender_4_out), .out(multiplier_3_out));  // open: cin, cout
  Multiplier #(.width(33)) multiplier_4 (
    .a(bit_extender_5_out), .b(bit_extender_6_out), .out(multiplier_4_out));  // open: cin, cout
  Multiplexer #(.select(4), .width(32)) multiplexer_3 (
    .in0(multiplexer_1_out), .in1(shifter_1_out), .in2(bit_extender_7_out), .in3(bit_extender_8_out),
    .in4(xor_1_out), .in5(multiplexer_2_out), .in6(or_1_out), .in7(and_1_out), .in8(multiplier_1_out),
    .in9(multiplier_2_out[31:0]), .in10(multiplier_3_out[31:0]), .in11(multiplier_4_out[31:0]),
    .in12(divider_1_out), .in13(divider_2_out), .in14(divider_1_rem), .in15(divider_2_rem), .out(Res),
    .sel(alu_ctrl_1_func));
endmodule

module alu_ctrl (
  input  [2:0] InstrFmt,
  input  [6:0] Func7,
  input  [2:0] Func3,
  input  Func3En,
  output Alt,
  output [3:0] Func
);

  PLA #(.in_width(14), .\table ("10000100000101 01\n1xxx0000001101 10\n11010100000101 01\n11010100000000 01\n0xxxxxxxxxxxxx 00")) pla_1 (
    .in({Func3En, Func3, Func7, InstrFmt}), .out({Func[3], Alt}));
  Multiplexer #(.width(3)) multiplexer_1 (.in0(3'b000), .in1(Func3), .out(Func[2:0]), .sel(Func3En));
endmodule

module register_file (
  input  [4:0] Rs1,
  input  [4:0] Rs2,
  input  RST,
  input  [31:0] DataIn,
  input  CLK,
  input  [4:0] Rd,
  input  We,
  output [31:0] Ra,
  output [31:0] Rb
);

  wire [31:0] decoder_1_out0, register_1_q, register_2_q, register_3_q, register_4_q, register_5_q,
       register_6_q, register_7_q, register_8_q, register_9_q, register_10_q, register_11_q, register_12_q,
       register_13_q, register_14_q, register_15_q, register_16_q, register_17_q, register_18_q,
       register_19_q, register_20_q, register_21_q, register_22_q, register_23_q, register_24_q,
       register_25_q, register_26_q, register_27_q, register_28_q, register_29_q, register_30_q,
       register_31_q;

  Multiplexer #(.select(5), .width(32)) multiplexer_1 (
    .in0({32{1'b0}}), .in1(register_29_q), .in2(register_27_q), .in3(register_25_q), .in4(register_24_q),
    .in5(register_21_q), .in6(register_19_q), .in7(register_16_q), .in8(register_17_q), .in9(register_13_q),
    .in10(register_11_q), .in11(register_9_q), .in12(register_8_q), .in13(register_5_q), .in14(register_3_q),
    .in15(register_1_q), .in16(register_31_q), .in17(register_30_q), .in18(register_28_q),
    .in19(register_26_q), .in20(register_23_q), .in21(register_22_q), .in22(register_20_q),
    .in23(register_18_q), .in24(register_15_q), .in25(register_14_q), .in26(register_12_q),
    .in27(register_10_q), .in28(register_7_q), .in29(register_6_q), .in30(register_4_q), .in31(register_2_q),
    .out(Ra), .sel(Rs1));
  Decoder #(.select(5)) decoder_1 (
    .out0(decoder_1_out0[0]), .out1(decoder_1_out0[1]), .out2(decoder_1_out0[2]), .out3(decoder_1_out0[3]),
    .out4(decoder_1_out0[4]), .out5(decoder_1_out0[5]), .out6(decoder_1_out0[6]), .out7(decoder_1_out0[7]),
    .out8(decoder_1_out0[8]), .out9(decoder_1_out0[9]), .out10(decoder_1_out0[10]),
    .out11(decoder_1_out0[11]), .out12(decoder_1_out0[12]), .out13(decoder_1_out0[13]),
    .out14(decoder_1_out0[14]), .out15(decoder_1_out0[15]), .out16(decoder_1_out0[16]),
    .out17(decoder_1_out0[17]), .out18(decoder_1_out0[18]), .out19(decoder_1_out0[19]),
    .out20(decoder_1_out0[20]), .out21(decoder_1_out0[21]), .out22(decoder_1_out0[22]),
    .out23(decoder_1_out0[23]), .out24(decoder_1_out0[24]), .out25(decoder_1_out0[25]),
    .out26(decoder_1_out0[26]), .out27(decoder_1_out0[27]), .out28(decoder_1_out0[28]),
    .out29(decoder_1_out0[29]), .out30(decoder_1_out0[30]), .out31(decoder_1_out0[31]), .sel(Rd), .en(We));
  Register #(.trigger("falling"), .width(32)) register_1 (
    .D(DataIn), .en(decoder_1_out0[15]), .Q(register_1_q), .clk(CLK), .clr(RST));
  Register #(.trigger("falling"), .width(32)) register_2 (
    .D(DataIn), .en(decoder_1_out0[31]), .Q(register_2_q), .clk(CLK), .clr(RST));
  Register #(.trigger("falling"), .width(32)) register_3 (
    .D(DataIn), .en(decoder_1_out0[14]), .Q(register_3_q), .clk(CLK), .clr(RST));
  Register #(.trigger("falling"), .width(32)) register_4 (
    .D(DataIn), .en(decoder_1_out0[30]), .Q(register_4_q), .clk(CLK), .clr(RST));
  Register #(.trigger("falling"), .width(32)) register_5 (
    .D(DataIn), .en(decoder_1_out0[13]), .Q(register_5_q), .clk(CLK), .clr(RST));
  Register #(.trigger("falling"), .width(32)) register_6 (
    .D(DataIn), .en(decoder_1_out0[29]), .Q(register_6_q), .clk(CLK), .clr(RST));
  Register #(.trigger("falling"), .width(32)) register_7 (
    .D(DataIn), .en(decoder_1_out0[28]), .Q(register_7_q), .clk(CLK), .clr(RST));
  Register #(.trigger("falling"), .width(32)) register_8 (
    .D(DataIn), .en(decoder_1_out0[12]), .Q(register_8_q), .clk(CLK), .clr(RST));
  Register #(.trigger("falling"), .width(32)) register_9 (
    .D(DataIn), .en(decoder_1_out0[11]), .Q(register_9_q), .clk(CLK), .clr(RST));
  Register #(.trigger("falling"), .width(32)) register_10 (
    .D(DataIn), .en(decoder_1_out0[27]), .Q(register_10_q), .clk(CLK), .clr(RST));
  Register #(.trigger("falling"), .width(32)) register_11 (
    .D(DataIn), .en(decoder_1_out0[10]), .Q(register_11_q), .clk(CLK), .clr(RST));
  Register #(.trigger("falling"), .width(32)) register_12 (
    .D(DataIn), .en(decoder_1_out0[26]), .Q(register_12_q), .clk(CLK), .clr(RST));
  Register #(.trigger("falling"), .width(32)) register_13 (
    .D(DataIn), .en(decoder_1_out0[9]), .Q(register_13_q), .clk(CLK), .clr(RST));
  Register #(.trigger("falling"), .width(32)) register_14 (
    .D(DataIn), .en(decoder_1_out0[25]), .Q(register_14_q), .clk(CLK), .clr(RST));
  Register #(.trigger("falling"), .width(32)) register_15 (
    .D(DataIn), .en(decoder_1_out0[24]), .Q(register_15_q), .clk(CLK), .clr(RST));
  Register #(.trigger("falling"), .width(32)) register_16 (
    .D(DataIn), .en(decoder_1_out0[7]), .Q(register_16_q), .clk(CLK), .clr(RST));
  Register #(.trigger("falling"), .width(32)) register_17 (
    .D(DataIn), .en(decoder_1_out0[8]), .Q(register_17_q), .clk(CLK), .clr(RST));
  Register #(.trigger("falling"), .width(32)) register_18 (
    .D(DataIn), .en(decoder_1_out0[23]), .Q(register_18_q), .clk(CLK), .clr(RST));
  Register #(.trigger("falling"), .width(32)) register_19 (
    .D(DataIn), .en(decoder_1_out0[6]), .Q(register_19_q), .clk(CLK), .clr(RST));
  Register #(.trigger("falling"), .width(32)) register_20 (
    .D(DataIn), .en(decoder_1_out0[22]), .Q(register_20_q), .clk(CLK), .clr(RST));
  Register #(.trigger("falling"), .width(32)) register_21 (
    .D(DataIn), .en(decoder_1_out0[5]), .Q(register_21_q), .clk(CLK), .clr(RST));
  Register #(.trigger("falling"), .width(32)) register_22 (
    .D(DataIn), .en(decoder_1_out0[21]), .Q(register_22_q), .clk(CLK), .clr(RST));
  Register #(.trigger("falling"), .width(32)) register_23 (
    .D(DataIn), .en(decoder_1_out0[20]), .Q(register_23_q), .clk(CLK), .clr(RST));
  Register #(.trigger("falling"), .width(32)) register_24 (
    .D(DataIn), .en(decoder_1_out0[4]), .Q(register_24_q), .clk(CLK), .clr(RST));
  Register #(.trigger("falling"), .width(32)) register_25 (
    .D(DataIn), .en(decoder_1_out0[3]), .Q(register_25_q), .clk(CLK), .clr(RST));
  Register #(.trigger("falling"), .width(32)) register_26 (
    .D(DataIn), .en(decoder_1_out0[19]), .Q(register_26_q), .clk(CLK), .clr(RST));
  Register #(.trigger("falling"), .width(32)) register_27 (
    .D(DataIn), .en(decoder_1_out0[2]), .Q(register_27_q), .clk(CLK), .clr(RST));
  Register #(.trigger("falling"), .width(32)) register_28 (
    .D(DataIn), .en(decoder_1_out0[18]), .Q(register_28_q), .clk(CLK), .clr(RST));
  Register #(.trigger("falling"), .width(32)) register_29 (
    .D(DataIn), .en(decoder_1_out0[1]), .Q(register_29_q), .clk(CLK), .clr(RST));
  Register #(.trigger("falling"), .width(32)) register_30 (
    .D(DataIn), .en(decoder_1_out0[17]), .Q(register_30_q), .clk(CLK), .clr(RST));
  Register #(.trigger("falling"), .width(32)) register_31 (
    .D(DataIn), .en(decoder_1_out0[16]), .Q(register_31_q), .clk(CLK), .clr(RST));
  Multiplexer #(.select(5), .width(32)) multiplexer_2 (
    .in0({32{1'b0}}), .in1(register_29_q), .in2(register_27_q), .in3(register_25_q), .in4(register_24_q),
    .in5(register_21_q), .in6(register_19_q), .in7(register_16_q), .in8(register_17_q), .in9(register_13_q),
    .in10(register_11_q), .in11(register_9_q), .in12(register_8_q), .in13(register_5_q), .in14(register_3_q),
    .in15(register_1_q), .in16(register_31_q), .in17(register_30_q), .in18(register_28_q),
    .in19(register_26_q), .in20(register_23_q), .in21(register_22_q), .in22(register_20_q),
    .in23(register_18_q), .in24(register_15_q), .in25(register_14_q), .in26(register_12_q),
    .in27(register_10_q), .in28(register_7_q), .in29(register_6_q), .in30(register_4_q), .in31(register_2_q),
    .out(Rb), .sel(Rs2));
endmodule

module mc_decode_control (
  input  [31:0] InstrIn,
  input  CLK,
  input  RST,
  output [31:0] Instr,
  output [6:0] Func7,
  output [4:0] Rs2,
  output [4:0] Rs1,
  output [2:0] Func3,
  output [4:0] Rd,
  output PcLd,
  output [2:0] InstrFmt,
  output JP,
  output BR,
  output [1:0] RFSrc,
  output RFWe,
  output ExFunc3En,
  output OprA,
  output OprB,
  output AddrSrc,
  output RW
);

  wire [0:0] mc_usequencer_1_ctrlword;

  Register #(.trigger("falling"), .width(32)) IR (
    .D(InstrIn), .en(mc_usequencer_1_ctrlword[0]), .Q({Func7, Instr[24:15], Func3, Instr[11:0]}), .clk(CLK),
    .clr(RST));
  mc_uSequencer mc_usequencer_1 (
    .CLK(CLK), .RST(RST), .Instr(Instr[6:0]),
    .CtrlWord({RW, AddrSrc, OprB, OprA, ExFunc3En, RFWe, RFSrc, BR, JP, InstrFmt, PcLd, mc_usequencer_1_ctrlword[0]}));

  assign {Instr[31:25], Instr[14:12]} = {Func7, Func3};
  assign Rd = Instr[11:7];
  assign Rs1 = Instr[19:15];
  assign Rs2 = Instr[24:20];
endmodule

module sc_decode_control (
  input  [31:0] InstrIn,
  input  CLK,
  input  RST,
  output [2:0] InstrFmt,
  output JP,
  output BR,
  output [1:0] RFSrc,
  output RFWe,
  output ExFunc3En,
  output OprA,
  output OprB,
  output AddrSrc,
  output RW,
  output [4:0] Rd,
  output [2:0] Func3,
  output [4:0] Rs1,
  output [4:0] Rs2,
  output [6:0] Func7,
  output [31:0] Instr
);

  wire [31:0] multiplexer_1_out;

  Register #(.width(32)) register_1 (
    .D(multiplexer_1_out), .Q({Func7, Instr[24:15], Func3, Instr[11:0]}), .clk(CLK), .clr(RST));  // open: en
  Multiplexer #(.width(32)) multiplexer_1 (.in0(InstrIn), .in1(32'h13), .out(multiplexer_1_out), .sel(AddrSrc));
  PLA #(.in_width(7), .out_width(13), .\table ("0110111 0010011100011 # LUI\n0010111 0011011000011 # AUIPC\n1101111 0011010101100 # JAL\n1100111 0010110101000 # JALR\n1100011 0011000010010 # BXX\n0000011 0110010000000 # LX\n0100011 1110000000001 # SX\n0010011 0010111000000 # RI\n0110011 0000111000101 # RR")) pla_1 (
    .in(Instr[6:0]), .out({RW, AddrSrc, OprB, OprA, ExFunc3En, RFWe, RFSrc, BR, JP, InstrFmt}));

  assign {Instr[31:25], Instr[14:12]} = {Func7, Func3};
  assign Rd = Instr[11:7];
  assign Rs1 = Instr[19:15];
  assign Rs2 = Instr[24:20];

  // Notes on the sheet:
  //   Nop
endmodule

module fwd_mux (
  input  [31:0] Opr1,
  input  [31:0] FwdData,
  input  FwdEn,
  input  [31:0] Opr2,
  input  ForceOpr2,
  output [31:0] BROpr,
  output [31:0] AluOpr
);

  Multiplexer #(.width(32)) multiplexer_1 (.in0(Opr1), .in1(FwdData), .out(BROpr), .sel(FwdEn));
  Multiplexer #(.width(32)) multiplexer_2 (.in0(BROpr), .in1(Opr2), .out(AluOpr), .sel(ForceOpr2));
endmodule

module fwd_cmp (
  input  [4:0] Rd,
  input  [4:0] Rs,
  output Fwd
);

  wire comparator_1_eq, comparator_2_eq;

  Comparator #(.mode("unsigned"), .width(5)) comparator_1 (.a(Rd), .b(Rs), .eq(comparator_1_eq));  // open: gt, lt
  and and_1 (Fwd, comparator_1_eq, ~comparator_2_eq);  // AND_Gate
  Comparator #(.mode("unsigned"), .width(5)) comparator_2 (
    .a(Rd), .b({5{1'b0}}), .eq(comparator_2_eq));  // open: gt, lt
endmodule

module forwarding_unit (
  input  [31:0] WBData,
  input  [31:0] MAData,
  input  [4:0] Rs1,
  input  [4:0] WB_Rd,
  input  [4:0] MA_Rd,
  input  [4:0] Rs2,
  input  WB_RFWe,
  input  MA_RFWe,
  output [31:0] A,
  output [31:0] B,
  output FwdA,
  output FwdB
);

  wire and_1_out, and_2_out, and_3_out, and_4_out, fwd_cmp_1_fwd, fwd_cmp_2_fwd, fwd_cmp_3_fwd, fwd_cmp_4_fwd;

  fwd_cmp fwd_cmp_1 (.Rd(Rs1), .Rs(WB_Rd), .Fwd(fwd_cmp_1_fwd));
  fwd_cmp fwd_cmp_2 (.Rd(MA_Rd), .Rs(Rs1), .Fwd(fwd_cmp_2_fwd));
  fwd_cmp fwd_cmp_3 (.Rd(WB_Rd), .Rs(Rs2), .Fwd(fwd_cmp_3_fwd));
  fwd_cmp fwd_cmp_4 (.Rd(MA_Rd), .Rs(Rs2), .Fwd(fwd_cmp_4_fwd));
  Multiplexer #(.width(32)) multiplexer_1 (.in0(WBData), .in1(MAData), .out(A), .sel(and_2_out));
  Multiplexer #(.width(32)) multiplexer_2 (.in0(WBData), .in1(MAData), .out(B), .sel(and_4_out));
  and and_1 (and_1_out, fwd_cmp_1_fwd, WB_RFWe);
  and and_2 (and_2_out, fwd_cmp_2_fwd, MA_RFWe);
  and and_3 (and_3_out, fwd_cmp_3_fwd, WB_RFWe);
  and and_4 (and_4_out, fwd_cmp_4_fwd, MA_RFWe);
  or or_1 (FwdA, and_1_out, and_2_out);
  or or_2 (FwdB, and_3_out, and_4_out);
endmodule

module branch_comparator (
  input  [31:0] A,
  input  [31:0] B,
  input  [2:0] Func3,
  output TK
);

  wire comparator_1_eq, comparator_1_gt, comparator_1_lt, comparator_2_eq, comparator_2_gt, comparator_2_lt,
       not_1_out, or_1_out, or_2_out;

  Comparator #(.width(32)) comparator_1 (
    .a(A), .b(B), .gt(comparator_1_gt), .eq(comparator_1_eq), .lt(comparator_1_lt));
  Comparator #(.mode("unsigned"), .width(32)) comparator_2 (
    .a(A), .b(B), .gt(comparator_2_gt), .eq(comparator_2_eq), .lt(comparator_2_lt));
  or or_1 (or_1_out, comparator_2_eq, comparator_2_gt);
  not not_1 (not_1_out, comparator_1_eq);
  or or_2 (or_2_out, comparator_1_eq, comparator_1_gt);
  Multiplexer #(.select(3)) multiplexer_1 (
    .in0(comparator_1_eq), .in1(not_1_out), .in2(1'b0), .in3(1'b0), .in4(comparator_1_lt), .in5(or_2_out),
    .in6(comparator_2_lt), .in7(or_1_out), .out(TK), .sel(Func3));
endmodule

module imm_gen (
  input  [31:0] Instr,
  input  [2:0] InstrFmt,
  output [31:0] Imm
);

  wire [11:0] bit_extender_4_out;
  wire [19:0] bit_extender_3_out;
  wire [20:0] bit_extender_1_out, bit_extender_2_out;

  assign bit_extender_1_out = {{20{Instr[31]}}, Instr[31]};  // Bit_Extender bit_extender_1
  assign bit_extender_2_out = {{20{Instr[31]}}, Instr[31]};  // Bit_Extender bit_extender_2
  assign bit_extender_3_out = {{19{Instr[31]}}, Instr[31]};  // Bit_Extender bit_extender_3
  assign bit_extender_4_out = {{11{Instr[31]}}, Instr[31]};  // Bit_Extender bit_extender_4
  Multiplexer #(.select(3), .width(32)) multiplexer_1 (
    .in0({bit_extender_1_out, Instr[30:20]}), .in1({bit_extender_2_out, Instr[30:25], Instr[11:7]}),
    .in2({bit_extender_3_out, Instr[7], Instr[30:25], Instr[11:8], 1'b0}), .in3({Instr[31:12], {12{1'b0}}}),
    .in4({bit_extender_4_out, Instr[19:12], Instr[20], Instr[30:21], 1'b0}), .in5({32{1'b0}}),
    .in6({32{1'b0}}), .in7({32{1'b0}}), .out(Imm), .sel(InstrFmt));

  // Notes on the sheet:
  //   I
  //   S
  //   B
  //   U
  //   J
endmodule

module pipe_if_de (
  input  [31:0] InstrIn,
  input  AddrSrc,
  input  [31:0] PCIn,
  input  [31:0] NPCIn,
  input  CLK,
  input  RST,
  output [31:0] Instr,
  output [4:0] Rs1,
  output [4:0] Rs2,
  output [31:0] PC,
  output [31:0] NPC
);

  wire [31:0] multiplexer_1_out;

  Multiplexer #(.width(32)) multiplexer_1 (.in0(InstrIn), .in1(32'h13), .out(multiplexer_1_out), .sel(AddrSrc));
  Register #(.width(32)) register_1 (.D(multiplexer_1_out), .Q(Instr), .clk(CLK), .clr(RST));  // open: en
  Register #(.width(32)) register_2 (.D(PCIn), .Q(PC), .clk(CLK), .clr(RST));  // open: en
  Register #(.width(32)) register_3 (.D(NPCIn), .Q(NPC), .clk(CLK), .clr(RST));  // open: en

  assign Rs1 = Instr[19:15];
  assign Rs2 = Instr[24:20];

  // Notes on the sheet:
  //   Nop
endmodule

module pipe_de_ex (
  input  [31:0] RaIn,
  input  [31:0] RbIn,
  input  [31:0] Instr,
  input  [31:0] PCIn,
  input  [31:0] NPCIn,
  input  [31:0] ImmIn,
  input  [12:0] CtrlWordIn,
  input  CLK,
  input  RST,
  output [31:0] Ra,
  output [31:0] Rb,
  output [4:0] Rd,
  output [2:0] Func3,
  output [4:0] Rs1,
  output [4:0] Rs2,
  output [6:0] Func7,
  output [31:0] PC,
  output [31:0] NPC,
  output [31:0] Imm,
  output [12:0] CtrlWord,
  output [2:0] InstrFmt,
  output JP,
  output BR,
  output ExFunc3En,
  output OprA,
  output OprB
);

  wire [6:0] register_3_q;

  Register #(.width(32)) register_1 (.D(RaIn), .Q(Ra), .clk(CLK), .clr(RST));  // open: en
  Register #(.width(32)) register_2 (.D(RbIn), .Q(Rb), .clk(CLK), .clr(RST));  // open: en
  Register #(.width(32)) register_3 (
    .D(Instr), .Q({Func7, Rs2, Rs1, Func3, Rd, register_3_q}), .clk(CLK), .clr(RST));  // open: en
  Register #(.width(32)) register_4 (.D(PCIn), .Q(PC), .clk(CLK), .clr(RST));  // open: en
  Register #(.width(32)) register_5 (.D(NPCIn), .Q(NPC), .clk(CLK), .clr(RST));  // open: en
  Register #(.width(32)) register_6 (.D(ImmIn), .Q(Imm), .clk(CLK), .clr(RST));  // open: en
  Register #(.width(13)) register_7 (
    .D(CtrlWordIn), .Q({CtrlWord[12:5], BR, CtrlWord[3:0]}), .clk(CLK), .clr(RST));  // open: en

  assign CtrlWord[4] = BR;
  assign ExFunc3En = CtrlWord[8];
  assign InstrFmt = CtrlWord[2:0];
  assign JP = CtrlWord[3];
  assign OprA = CtrlWord[9];
  assign OprB = CtrlWord[10];
endmodule

module bp_pipe_de_ex (
  input  [31:0] RaIn,
  input  [31:0] RbIn,
  input  [31:0] Instr,
  input  [31:0] PCIn,
  input  [31:0] NPCIn,
  input  [31:0] ImmIn,
  input  [12:0] CtrlWordIn,
  input  CLK,
  input  RST,
  output [31:0] Ra,
  output [31:0] Rb,
  output [4:0] Rd,
  output [2:0] Func3,
  output [4:0] Rs1,
  output [4:0] Rs2,
  output [6:0] Func7,
  output [31:0] PC,
  output [31:0] NPC,
  output [31:0] Imm,
  output [12:0] CtrlWord,
  output [2:0] InstrFmt,
  output ExFunc3En,
  output OprA,
  output OprB
);

  wire [6:0] register_3_q;

  Register #(.width(32)) register_1 (.D(RaIn), .Q(Ra), .clk(CLK), .clr(RST));  // open: en
  Register #(.width(32)) register_2 (.D(RbIn), .Q(Rb), .clk(CLK), .clr(RST));  // open: en
  Register #(.width(32)) register_3 (
    .D(Instr), .Q({Func7, Rs2, Rs1, Func3, Rd, register_3_q}), .clk(CLK), .clr(RST));  // open: en
  Register #(.width(32)) register_4 (.D(PCIn), .Q(PC), .clk(CLK), .clr(RST));  // open: en
  Register #(.width(32)) register_5 (.D(NPCIn), .Q(NPC), .clk(CLK), .clr(RST));  // open: en
  Register #(.width(32)) register_6 (.D(ImmIn), .Q(Imm), .clk(CLK), .clr(RST));  // open: en
  Register #(.width(13)) register_7 (.D(CtrlWordIn), .Q(CtrlWord), .clk(CLK), .clr(RST));  // open: en

  assign ExFunc3En = CtrlWord[8];
  assign InstrFmt = CtrlWord[2:0];
  assign OprA = CtrlWord[9];
  assign OprB = CtrlWord[10];
endmodule

module pipe_ex_ma (
  input  JP_BR_In,
  input  [31:0] AluResIn,
  input  [2:0] Func3In,
  input  [31:0] RbIn,
  input  [31:0] NPCIn,
  input  [31:0] ImmIn,
  input  [4:0] RdIn,
  input  [12:0] CtrlWordIn,
  input  CLK,
  input  RST,
  output JP_BR,
  output [31:0] AluRes,
  output [2:0] Func3,
  output [31:0] Rb,
  output [31:0] NPC,
  output [31:0] Imm,
  output [4:0] Rd,
  output [12:0] CtrlWord,
  output AddrSrc,
  output RW,
  output RfWe,
  output lui
);

  Register #(.width(1)) register_1 (.D(JP_BR_In), .Q(JP_BR), .clk(CLK), .clr(RST));  // open: en
  Register #(.width(32)) register_2 (.D(AluResIn), .Q(AluRes), .clk(CLK), .clr(RST));  // open: en
  Register #(.width(3)) register_3 (.D(Func3In), .Q(Func3), .clk(CLK), .clr(RST));  // open: en
  Register #(.width(32)) register_4 (.D(RbIn), .Q(Rb), .clk(CLK), .clr(RST));  // open: en
  Register #(.width(32)) register_5 (.D(NPCIn), .Q(NPC), .clk(CLK), .clr(RST));  // open: en
  Register #(.width(32)) register_6 (.D(ImmIn), .Q(Imm), .clk(CLK), .clr(RST));  // open: en
  Register #(.width(5)) register_7 (.D(RdIn), .Q(Rd), .clk(CLK), .clr(RST));  // open: en
  Register #(.width(13)) register_8 (
    .D(CtrlWordIn), .Q({CtrlWord[12], AddrSrc, CtrlWord[10:0]}), .clk(CLK), .clr(RST));  // open: en
  and and_1 (lui, CtrlWord[5], CtrlWord[6]);

  assign CtrlWord[11] = AddrSrc;
  assign RfWe = CtrlWord[7];
  assign RW = CtrlWord[12];
endmodule

module bp_pipe_ex_ma (
  input  BranchTakenIn,
  input  [31:0] AluResIn,
  input  [2:0] Func3In,
  input  [31:0] RbIn,
  input  [31:0] NPCIn,
  input  [31:0] ImmIn,
  input  [4:0] RdIn,
  input  [31:0] PCIn,
  input  [12:0] CtrlWordIn,
  input  CLK,
  input  RST,
  output BranchTaken,
  output [31:0] AluRes,
  output [2:0] Func3,
  output [31:0] Rb,
  output [31:0] NPC,
  output [31:0] Imm,
  output [4:0] Rd,
  output [31:0] PC,
  output BR,
  output [12:0] CtrlWord,
  output Eval_JP_BR,
  output AddrSrc,
  output RW,
  output RfWe,
  output lui
);

  Register #(.width(1)) register_1 (.D(BranchTakenIn), .Q(BranchTaken), .clk(CLK), .clr(RST));  // open: en
  Register #(.width(32)) register_2 (.D(AluResIn), .Q(AluRes), .clk(CLK), .clr(RST));  // open: en
  Register #(.width(3)) register_3 (.D(Func3In), .Q(Func3), .clk(CLK), .clr(RST));  // open: en
  Register #(.width(32)) register_4 (.D(RbIn), .Q(Rb), .clk(CLK), .clr(RST));  // open: en
  Register #(.width(32)) register_5 (.D(NPCIn), .Q(NPC), .clk(CLK), .clr(RST));  // open: en
  Register #(.width(32)) register_6 (.D(ImmIn), .Q(Imm), .clk(CLK), .clr(RST));  // open: en
  Register #(.width(5)) register_7 (.D(RdIn), .Q(Rd), .clk(CLK), .clr(RST));  // open: en
  Register #(.width(32)) register_8 (.D(PCIn), .Q(PC), .clk(CLK), .clr(RST));  // open: en
  Register #(.width(13)) register_9 (
    .D(CtrlWordIn), .Q({CtrlWord[12], AddrSrc, CtrlWord[10:5], BR, CtrlWord[3:0]}), .clk(CLK), .clr(RST));  // open: en
  or or_1 (Eval_JP_BR, CtrlWord[3], BR);
  and and_1 (lui, CtrlWord[5], CtrlWord[6]);

  assign {CtrlWord[11], CtrlWord[4]} = {AddrSrc, BR};
  assign RfWe = CtrlWord[7];
  assign RW = CtrlWord[12];
endmodule

module pipe_ma_wb (
  input  [31:0] MemDataIn,
  input  [31:0] AluResIn,
  input  [31:0] NPCIn,
  input  [31:0] ImmIn,
  input  [4:0] RdIn,
  input  [12:0] CtrlWordIn,
  input  CLK,
  input  RST,
  output [31:0] MemData,
  output [31:0] AluRes,
  output [31:0] NPC,
  output [31:0] Imm,
  output [4:0] Rd,
  output [1:0] RFSrc,
  output RFWe
);

  wire [12:0] register_6_q;

  Register #(.width(32)) register_1 (.D(MemDataIn), .Q(MemData), .clk(CLK), .clr(RST));  // open: en
  Register #(.width(32)) register_2 (.D(AluResIn), .Q(AluRes), .clk(CLK), .clr(RST));  // open: en
  Register #(.width(32)) register_3 (.D(NPCIn), .Q(NPC), .clk(CLK), .clr(RST));  // open: en
  Register #(.width(32)) register_4 (.D(ImmIn), .Q(Imm), .clk(CLK), .clr(RST));  // open: en
  Register #(.width(5)) register_5 (.D(RdIn), .Q(Rd), .clk(CLK), .clr(RST));  // open: en
  Register #(.width(13)) register_6 (
    .D(CtrlWordIn), .Q({register_6_q[12:8], RFWe, RFSrc, register_6_q[4:0]}), .clk(CLK), .clr(RST));  // open: en
endmodule

module pl_decode (
  input  [31:0] Instr,
  output [12:0] CtrlWord,
  output [31:0] Imm
);

  PLA #(.in_width(7), .out_width(13), .\table ("0110111 0010011100011 # LUI\n0010111 0011011000011 # AUIPC\n1101111 0011010101100 # JAL\n1100111 0010110101000 # JALR\n1100011 0011000010010 # BXX\n0000011 0110010000000 # LX\n0100011 1110000000001 # SX\n0010011 0010111000000 # RI\n0110011 0000111000101 # RR")) pla_1 (
    .in(Instr[6:0]), .out(CtrlWord));
  imm_gen imm_gen_1 (.InstrFmt(CtrlWord[2:0]), .Instr(Instr), .Imm(Imm));
endmodule

module data_aligner (
  input  [31:0] DataIn,
  input  [2:0] Func3,
  output [31:0] DataOut
);

  wire [31:0] bit_extender_1_out, bit_extender_2_out, bit_extender_3_out, bit_extender_4_out;

  Multiplexer #(.select(3), .width(32)) multiplexer_1 (
    .in0(bit_extender_1_out), .in1(bit_extender_2_out), .in2(DataIn), .in3({32{1'b0}}),
    .in4(bit_extender_3_out), .in5(bit_extender_4_out), .in6({32{1'b0}}), .in7({32{1'b0}}), .out(DataOut));  // open: sel
  assign bit_extender_1_out = {{24{DataIn[7]}}, DataIn[7:0]};  // Bit_Extender bit_extender_1
  assign bit_extender_2_out = {{16{DataIn[15]}}, DataIn[15:0]};  // Bit_Extender bit_extender_2
  assign bit_extender_3_out = {{24{1'b0}}, DataIn[7:0]};  // Bit_Extender bit_extender_3
  assign bit_extender_4_out = {{16{1'b0}}, DataIn[15:0]};  // Bit_Extender bit_extender_4
endmodule

module mc_hold_reg (
  input  [31:0] DataIn,
  input  CLK,
  input  RST,
  output [31:0] DataOut
);

  Register #(.width(32)) register_1 (.D(DataIn), .Q(DataOut), .clk(CLK), .clr(RST));  // open: en
endmodule

module mc_uSequencer (
  input  [6:0] Instr,
  input  CLK,
  input  RST,
  output [14:0] CtrlWord
);

  wire [1:0] pla_1_out;
  wire [6:0] multiplexer_1_out, uPC_q;

  Multiplexer #(.width(7)) multiplexer_1 (.in0({7{1'b0}}), .in1(Instr), .out(multiplexer_1_out), .sel(pla_1_out[1]));
  PLA #(.in_width(7), .out_width(17), .\table ("0000000 00000000000000111 # IF\n0110111 00100000000110000 # LUI-D\n0111000 00000111000001001 # LUI-W\n0010111 00110000000110000 # AUP-D\n0011000 00000000000110000 # AUP-E\n0011001 00000110000001001 # AUP-W\n1101111 00110000001000000 # JAL-D\n1110000 00000101011001001 # JAL-W\n1100111 00100000010000000 # JLR-D\n1101000 00001101011001001 # JLR-W\n1100011 00110000000100000 # BXX-D\n1100100 00000000100101001 # BXX-E\n0000011 00100000000000000 # LX-D\n0000100 00000000000000000 # LX-E\n0000101 01000000000000000 # LX-M\n0000110 00000100000001001 # LX-W\n0100011 00100000000010000 # SX-D\n0100100 00000000000010000 # SX-E\n0100101 11000000000001001 # SX-M\n0010011 00100000000000000 # RI-D\n0010100 00001000000000000 # RI-E\n0010101 00000110000001001 # RI-W\n0110011 00000000001010000 # RR-D\n0110100 00001000001010000 # RR-E\n0110101 00000110000001001 # RR-W")) pla_1 (
    .in(uPC_q), .out({CtrlWord, pla_1_out}));
  Counter #(.max('h7f), .width(7)) uPC (
    .load(pla_1_out[0]), .D(multiplexer_1_out), .Q(uPC_q), .clk(CLK), .clr(RST));  // open: count, carry, up
endmodule

module fetch_unit (
  input  [31:0] PCTarget,
  input  PC_Src,
  input  En,
  input  CLK,
  input  RST,
  output [31:0] NPC,
  output [31:0] PC
);

  wire [31:0] and_1_out, multiplexer_1_out;

  assign and_1_out = PCTarget & ~32'h1;  // AND_Gate and_1, 32 bits wide
  Multiplexer #(.width(32)) multiplexer_1 (.in0(NPC), .in1(and_1_out), .out(multiplexer_1_out), .sel(PC_Src));
  Register #(.trigger("falling"), .width(32)) register_1 (.D(multiplexer_1_out), .en(En), .Q(PC), .clk(CLK), .clr(RST));
  Adder #(.width(32)) adder_1 (.a(PC), .b(32'h4), .out(NPC));  // open: cin, cout
endmodule

module hold_unit (
  input  nRDY,
  input  Hold,
  input  RST,
  input  CLKIn,
  output HLDA,
  output CLK
);

  wire and_1_out, d_ff_1_qn, or_1_out;

  and and_1 (and_1_out, ~nRDY, CLKIn, Hold);  // AND_Gate
  D_Flip_Flop d_ff_1 (.Q(HLDA), .Qn(d_ff_1_qn), .preset(and_1_out), .reset(or_1_out));  // open: D, clk
  or or_1 (or_1_out, ~Hold, RST);  // OR_Gate
  and and_2 (CLK, d_ff_1_qn, CLKIn);
endmodule

module pipe_flush (
  input  JP_BR,
  input  Clk,
  input  Rst,
  output Flush
);

  wire d_ff_1_q;

  D_Flip_Flop #(.trigger("falling")) d_ff_1 (.D(JP_BR), .clk(Clk), .Q(d_ff_1_q), .reset(Flush));  // open: Qn, preset
  or or_1 (Flush, d_ff_1_q, Rst);
endmodule

module branch_predictor (
  input  [31:0] PC,
  input  [31:0] Eval_PC,
  input  [31:0] Alu_Res,
  input  Is_Branch,
  input  Is_Taken,
  input  Eval,
  input  CLK,
  input  RST,
  input  [31:0] NPC,
  output [31:0] Predicted_Target,
  output PC_Src,
  output Flush
);

  wire predictor_btb_1_eval_target_hit, predictor_btb_1_fetch_hit, predictor_coordinator_1_invalidate_btb,
       predictor_coordinator_1_update_btb;
  wire [5:0] predictor_bhsr_1_history;
  wire [31:0] predictor_btb_1_fetch_target;

  predictor_BHSR predictor_bhsr_1 (
    .En(Eval), .Is_Branch(Is_Branch), .Is_Taken(Is_Taken), .Clk(CLK), .Rst(RST),
    .History(predictor_bhsr_1_history));
  predictor_BTB predictor_btb_1 (
    .RST(RST), .We(predictor_coordinator_1_update_btb), .CLK(CLK),
    .Invalidate(predictor_coordinator_1_invalidate_btb), .BHSR(predictor_bhsr_1_history), .Curr_PC(PC),
    .Eval_PC(Eval_PC), .Alu_Res(Alu_Res), .Fetch_Hit(predictor_btb_1_fetch_hit),
    .Fetch_Target(predictor_btb_1_fetch_target), .Eval_Target_Hit(predictor_btb_1_eval_target_hit));
  predictor_coordinator predictor_coordinator_1 (
    .Fetch_Hit(predictor_btb_1_fetch_hit), .Eval_Target_Hit(predictor_btb_1_eval_target_hit),
    .Is_Branch(Is_Branch), .Is_Taken(Is_Taken), .Eval(Eval), .CLK(CLK), .RST(RST),
    .Fetch_Target(predictor_btb_1_fetch_target), .Alu_Res(Alu_Res), .NPC(NPC), .PC_Src(PC_Src),
    .Update_BTB(predictor_coordinator_1_update_btb), .Invalidate_BTB(predictor_coordinator_1_invalidate_btb),
    .Flush(Flush), .predicted_target(Predicted_Target));
endmodule

module predictor_coordinator (
  input  Fetch_Hit,
  input  Eval_Target_Hit,
  input  Is_Branch,
  input  Is_Taken,
  input  Eval,
  input  CLK,
  input  RST,
  input  [31:0] Fetch_Target,
  input  [31:0] Alu_Res,
  input  [31:0] NPC,
  output PC_Src,
  output Update_BTB,
  output Invalidate_BTB,
  output Flush,
  output [31:0] predicted_target
);

  wire d_ff_1_q;
  wire [5:3] pla_1_out;

  PLA #(.in_width(5), .out_width(6), .\table ("10101 000001 # FHT\n11111 000001 # FHT\n1110x 011011 # UPD\n1011x 101111 # INV\n1x00x 011011 # UPD\n1x011 000001 # FHT\n0xxx1 000001 # FHT")) pla_1 (
    .in({Eval, Is_Taken, Is_Branch, Eval_Target_Hit, Fetch_Hit}),
    .out({pla_1_out, Invalidate_BTB, Update_BTB, PC_Src}));
  D_Flip_Flop #(.trigger("falling")) d_ff_1 (
    .D(pla_1_out[3]), .clk(CLK), .Q(d_ff_1_q), .reset(Flush));  // open: Qn, preset
  Multiplexer #(.select(2), .width(32)) multiplexer_1 (
    .in0(Fetch_Target), .in1(Alu_Res), .in2(NPC), .in3({32{1'b0}}), .out(predicted_target),
    .sel(pla_1_out[5:4]));
  or or_1 (Flush, d_ff_1_q, RST);
endmodule

module predictor_BTB (
  input  RST,
  input  [31:0] Curr_PC,
  input  [5:0] BHSR,
  input  We,
  input  CLK,
  input  [31:0] Eval_PC,
  input  Invalidate,
  input  [31:0] Alu_Res,
  output Fetch_Hit,
  output [31:0] Fetch_Target,
  output Eval_Target_Hit
);

  wire comparator_1_eq, comparator_2_eq;
  wire [5:0] bit_extender_1_out, bit_extender_2_out, xor_1_out, xor_2_out;
  wire [31:0] multiplexer_1_out, ram_2_dout;
  wire [32:0] ram_1_dout;
  wire [32:32] not_1_out;

  Multiplexer #(.width(32)) multiplexer_1 (.in0(Curr_PC), .in1(Eval_PC), .out(multiplexer_1_out), .sel(We));
  not not_1 (not_1_out[32], Invalidate);
  Bit_Extender #(.in_width(30), .out_width(6)) bit_extender_1 (.in(multiplexer_1_out[31:2]), .out(bit_extender_1_out));
  Bit_Extender #(.in_width(30), .out_width(6)) bit_extender_2 (.in(Eval_PC[31:2]), .out(bit_extender_2_out));
  assign xor_1_out = bit_extender_1_out ^ BHSR;  // XOR_Gate xor_1, 6 bits wide
  assign xor_2_out = BHSR ^ bit_extender_2_out;  // XOR_Gate xor_2, 6 bits wide
  RAM #(.addrWidth(6), .clearpin("true"), .dataWidth(64), .enables("line")) ram_1 (
    .addr(xor_1_out), .we(We), .clk(CLK), .din({Alu_Res[31:1], not_1_out[32], Eval_PC}),
    .dout({Fetch_Target[31:1], ram_1_dout}), .clr(RST));
  RAM #(.addrWidth(6), .clearpin("true"), .dataWidth(32), .enables("line")) ram_2 (
    .addr(xor_2_out), .we(We), .clk(CLK), .din({Alu_Res[31:1], not_1_out[32]}), .dout(ram_2_dout), .clr(RST));
  Comparator #(.mode("unsigned"), .width(32)) comparator_1 (
    .a(Curr_PC), .b(ram_1_dout[31:0]), .eq(comparator_1_eq));  // open: gt, lt
  Comparator #(.mode("unsigned"), .width(32)) comparator_2 (
    .a({ram_2_dout[31:1], 1'b0}), .b(Alu_Res), .eq(comparator_2_eq));  // open: gt, lt
  and and_1 (Fetch_Hit, comparator_1_eq, ram_1_dout[32]);
  and and_2 (Eval_Target_Hit, ram_2_dout[0], comparator_2_eq);

  assign Fetch_Target[0] = 1'b0;
endmodule

module predictor_BHSR (
  input  En,
  input  Is_Branch,
  input  Is_Taken,
  input  Clk,
  input  Rst,
  output [5:0] History
);

  wire or_1_out;

  or or_1 (or_1_out, ~Is_Branch, Is_Taken);  // OR_Gate
  Shift_Register #(.length(6), .trigger("falling")) BHSR (
    .shift(En), .in(or_1_out), .clk(Clk), .out(History[0]), .clr(Rst), .q0(History[5]), .q1(History[4]),
    .q2(History[3]), .q3(History[2]), .q4(History[1]));  // open: load, d0, d1, d2, d3, d4, d5, q5
endmodule
